# Fritzing sketch sketch (saved by Fritzing 0.9.3b)
breadboards: 1

parts:
  Part5 = Micro Lipo Charger
  Matrix_keypad1 = KEYPAD 4x4
  Part2 = Adafruit HUZZAH ESP8266 [part_number="Adafruit #2471"]
  U1 = Battery Holders [package=lipo-1100mAh]  # not connected

nets:
  N1: Part5.VBAT, Part2.VBAT
  GND: Part5.GND, Part2.GND
  N2: Matrix_keypad1.col1, Part2.GPIO5
  N3: Matrix_keypad1.col2, Part2.GPIO4
  N4: Matrix_keypad1.col3, Part2.GPIO2
  N5: Matrix_keypad1.col4, Part2.GPIO15
  N6: Matrix_keypad1.row1, Part2.GPIO13
  N7: Matrix_keypad1.row2, Part2.GPIO12
  N8: Matrix_keypad1.row3, Part2.GPIO14
  N9: Matrix_keypad1.row4, Part2.GPIO16

custom parts:
  Micro Lipo Charger: Oh so handy, this little lipo charger is so small and easy to use you can keep it on your desk or mount it easily into any project! Simply plug it via any MicroUSB cable into a USB port and a 3.7V/4.2V lithium polymer or lithium ion rechargeable battery into the JST plug on the other end. There are two LEDs - one red and one green. While charging, the red LED is lit. When the battery is fully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
  KEYPAD 4x4: Matrix keypad 16 buttons, 4 rows x 4 columns
  Adafruit HUZZAH ESP8266: Add Internet to your next project with an adorable, bite-sized WiFi microcontroller, at a price you like! The ESP8266 processor from Espressif is an 80 MHz microcontroller with a full WiFi front-end (both as client and access point) and TCP/IP stack with DNS support as well. While this chip has been very popular, its also been very difficult to use. Most of the low cost modules are not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
